# Fritzing sketch wiring (saved by Fritzing 0.9.4)
circuit board: 10.1776cm x 5.36194cm
breadboards: 2

parts:
  SBUS_RECEIVER = Dagu DGServo 9g header (male) [package=THT]
  NPN = NPN-Transistor [part_number=BC337 package="TO92 [THT]"]
  ESC = Dagu DGServo 9g header (male) [package=THT]
  part = Resistor [tolerance=±5% resistance=4.7k package=THT]
  part_2 = Resistor [tolerance=±5% resistance=10k package=THT]
  Arduino_MEGA_R3_Quadcopter_Shield = Arduino Mega 2560 (Rev3)

nets:
  GND: SBUS_RECEIVER.gnd, NPN.E, ESC.gnd, Arduino_MEGA_R3_Quadcopter_Shield.GND
  VCC: SBUS_RECEIVER.Vcc, ESC.Vcc, part.Pin_0, Arduino_MEGA_R3_Quadcopter_Shield.5V
  N1: SBUS_RECEIVER.pulse, part_2.Pin_1
  N2: NPN.B, part_2.Pin_0
  N3: NPN.C, part.Pin_1, Arduino_MEGA_R3_Quadcopter_Shield.D19/RX1
  N4: ESC.pulse, Arduino_MEGA_R3_Quadcopter_Shield.D4_PWM
