# Fritzing sketch wiring (saved by Fritzing 0.9.4)
circuit board: 10.1776cm x 5.36194cm
breadboards: 1

parts:
  IMU = InvenSense MPU6050
  Arduino_MEGA_R3_Quadcopter_Shield = Arduino Mega 2560 (Rev3)

nets:
  VCC: IMU.VCC, Arduino_MEGA_R3_Quadcopter_Shield.5V
  GND: IMU.GND, Arduino_MEGA_R3_Quadcopter_Shield.GND
  N1: IMU.SCL, Arduino_MEGA_R3_Quadcopter_Shield.D21/SCL
  N2: IMU.SDA, Arduino_MEGA_R3_Quadcopter_Shield.D20/SDA
  N3: IMU.INT, Arduino_MEGA_R3_Quadcopter_Shield.D2_PWM

notes:
  CANAN v1.0
