# Fritzing sketch wiring (saved by Fritzing 0.9.4)
circuit board: 10.1776cm x 5.36194cm
breadboards: 2

parts:
  Motor_Right = Dagu DGServo 9g header (male) [package=THT]
  MPU6050 = InvenSense MPU6050
  Arduino_MEGA_R3_Quadcopter_Shield = Arduino Mega 2560 (Rev3)
  SBUS_RC = Dagu DGServo 9g header (male) [package=THT]
  NPN = NPN-Transistor [part_number=BC337 package="TO92 [THT]"]
  Motor_Left = Dagu DGServo 9g header (male) [package=THT]
  part = Resistor [tolerance=±5% resistance=4.7k package=THT]
  part_2 = Resistor [tolerance=±5% resistance=10k package=THT]

nets:
  GND: Motor_Right.gnd, MPU6050.GND, Arduino_MEGA_R3_Quadcopter_Shield.GND, SBUS_RC.gnd, NPN.E, Motor_Left.gnd
  VCC: Motor_Right.Vcc, MPU6050.VCC, Arduino_MEGA_R3_Quadcopter_Shield.5V, SBUS_RC.Vcc, Motor_Left.Vcc, part.Pin_0
  N1: Motor_Right.pulse, Arduino_MEGA_R3_Quadcopter_Shield.D5_PWM
  N2: MPU6050.SCL, Arduino_MEGA_R3_Quadcopter_Shield.D21/SCL
  N3: MPU6050.SDA, Arduino_MEGA_R3_Quadcopter_Shield.D20/SDA
  N4: MPU6050.INT, Arduino_MEGA_R3_Quadcopter_Shield.D2_PWM
  N5: Arduino_MEGA_R3_Quadcopter_Shield.D19/RX1, NPN.C, part.Pin_1
  N6: Arduino_MEGA_R3_Quadcopter_Shield.D4_PWM, Motor_Left.pulse
  N7: SBUS_RC.pulse, part_2.Pin_1
  N8: NPN.B, part_2.Pin_0

notes:
  CANAN v1.0
