# Fritzing sketch arduino drone pcb Sketch (saved by Fritzing 0.9.4)
circuit board: 10.1776cm x 5.36194cm
breadboards: 3

parts:
  Bluetooth = female pin header, 4 pins [form="♀ (female)"]
  Motor_1 = Dagu DGServo 9g header (male) [package=THT]
  Motor_3 = Dagu DGServo 9g header (male) [package=THT]
  IMU = InvenSense MPU6050
  Motor_2 = Dagu DGServo 9g header (male) [package=THT]
  Led = LED - 5mm [color="Red (633nm)" package="5 mm [THT]"]
  Barometer = female pin header, 7 pins [form="♀ (female)" part_number=ms5661]
  Arduino_MEGA_R3_Quadcopter_Shield = Arduino Mega 2560 (Rev3)
  SBUS_RC = Dagu DGServo 9g header (male) [package=THT]
  Buzzer = Piezo Speaker
  NPN = NPN-Transistor [part_number=BC337 package="TO92 [THT]"]
  Motor_4 = Dagu DGServo 9g header (male) [package=THT]
  220Ω = Resistor [tolerance=±5% resistance=220 package=THT]
  220Ω_2 = Resistor [tolerance=±5% resistance=220 package=THT]
  4_7kΩ = Resistor [tolerance=±5% resistance=4.7k package=THT]
  10kΩ = Resistor [tolerance=±5% resistance=10k package=THT]

nets:
  N1: Bluetooth.pin1, Arduino_MEGA_R3_Quadcopter_Shield.D16_PWM/TX2
  N2: Bluetooth.pin2, Arduino_MEGA_R3_Quadcopter_Shield.D17_PWM/RX2
  GND: Bluetooth.pin3, Motor_1.gnd, Motor_3.gnd, IMU.GND, Motor_2.gnd, Led.cathode, Barometer.pin2, Arduino_MEGA_R3_Quadcopter_Shield.GND, SBUS_RC.gnd, Buzzer.pin1, NPN.E, Motor_4.gnd
  VCC: Bluetooth.pin4, Motor_1.Vcc, Motor_3.Vcc, IMU.VCC, Motor_2.Vcc, Barometer.pin1, Arduino_MEGA_R3_Quadcopter_Shield.5V, SBUS_RC.Vcc, Motor_4.Vcc, 4_7kΩ.Pin_0
  N3: Motor_1.pulse, Arduino_MEGA_R3_Quadcopter_Shield.D7_PWM
  N4: Motor_3.pulse, Arduino_MEGA_R3_Quadcopter_Shield.D5_PWM
  N5: IMU.SCL, Barometer.pin3, Arduino_MEGA_R3_Quadcopter_Shield.D21/SCL, Arduino_MEGA_R3_Quadcopter_Shield.SCL
  N6: IMU.SDA, Barometer.pin4, Arduino_MEGA_R3_Quadcopter_Shield.D20/SDA, Arduino_MEGA_R3_Quadcopter_Shield.SDA
  N7: IMU.INT, Arduino_MEGA_R3_Quadcopter_Shield.D2_PWM
  N8: Motor_2.pulse, Arduino_MEGA_R3_Quadcopter_Shield.D6_PWM
  N9: Led.anode, 220Ω.Pin_0
  N10: Arduino_MEGA_R3_Quadcopter_Shield.D19/RX1, NPN.C, 4_7kΩ.Pin_1
  N11: Arduino_MEGA_R3_Quadcopter_Shield.D13_PWM, 220Ω.Pin_1
  N12: Arduino_MEGA_R3_Quadcopter_Shield.D12_PWM, 220Ω_2.Pin_1
  N13: Arduino_MEGA_R3_Quadcopter_Shield.D4_PWM, Motor_4.pulse
  N14: SBUS_RC.pulse, 10kΩ.Pin_1
  N15: Buzzer.pin2, 220Ω_2.Pin_0
  N16: NPN.B, 10kΩ.Pin_0

notes:
  CANAN v1.0
  Berkay'la Elektronik
